// Logisim project lab4.1.circ as structural Verilog
module mian (
  input  x1,
  input  x2,
  input  x3,
  output Y0,
  output Y1,
  output Y2,
  output Y3,
  output Y4,
  output Y5,
  output Y6,
  output Y7
);

  wire not_1_out, not_2_out, not_3_out;

  not not_1 (not_1_out, x1);
  not not_2 (not_2_out, x2);
  not not_3 (not_3_out, x3);
  and and_1 (Y0, not_3_out, not_2_out, not_1_out);
  and and_2 (Y1, not_3_out, not_2_out, x1);
  and and_3 (Y2, not_3_out, x2, not_1_out);
  and and_4 (Y3, not_3_out, x2, x1);
  and and_5 (Y4, x3, not_2_out, not_1_out);
  and and_6 (Y5, x3, not_2_out, x1);
  and and_7 (Y6, x3, x2, not_1_out);
  and and_8 (Y7, x3, x2, x1);
endmodule
