// Logisim project lab4.3.circ as structural Verilog: 1 circuit, main circuit main
module main (
  input  x1,
  input  x2,
  input  x3,
  input  x4,
  output Y0,
  output Y1,
  output Y2,
  output Y3,
  output Y4,
  output Y5,
  output Y6,
  output Y7,
  output Y8,
  output Y9,
  output Y10,
  output Y11,
  output Y12,
  output Y13,
  output Y14,
  output Y15
);

  wire not_1_out, not_2_out, not_3_out, not_4_out;

  not not_1 (not_1_out, x1);
  not not_2 (not_2_out, x2);
  not not_3 (not_3_out, x3);
  not not_4 (not_4_out, x4);
  and and_1 (Y0, x1, x2, x3, x4);
  and and_2 (Y1, x1, x2, x3, not_4_out);
  and and_3 (Y2, x1, x2, not_3_out, x4);
  and and_4 (Y3, x1, x2, not_3_out, not_4_out);
  and and_5 (Y4, x1, not_2_out, x3, x4);
  and and_6 (Y5, x1, not_2_out, x3, not_4_out);
  and and_7 (Y6, x1, not_2_out, not_3_out, x4);
  and and_8 (Y7, x1, not_2_out, not_3_out, not_4_out);
  and and_9 (Y8, not_1_out, x2, x3, x4);
  and and_10 (Y9, not_1_out, x2, x3, not_4_out);
  and and_11 (Y10, not_1_out, x2, not_3_out, x4);
  and and_12 (Y11, not_1_out, x2, not_3_out, not_4_out);
  and and_13 (Y12, not_1_out, not_2_out, x3, x4);
  and and_14 (Y13, not_1_out, not_2_out, x3, not_4_out);
  and and_15 (Y14, not_1_out, not_2_out, not_3_out, x4);
  and and_16 (Y15, not_1_out, not_2_out, not_3_out, not_4_out);
endmodule
